# Fritzing sketch BCA182-Multisensor-Schematic (saved by Fritzing 1.0.4)
breadboards: 1

parts:
  M1 = STM32F103C8T6 blue mini board
  DHT22 = Header 4 [package=1x04-smd]
  SSD1306_OLED = Header 4 [package=1x04-smd]  # not connected
  Buzzer = Piezo Speaker
  PIR_sensor = Header 3 [package=1x03-1mm-ra]
  LDR_module = Header 3 [package=1x03-1mm-ra]  # not connected
  KY-040_encoder = Header 4 [package=1x04-smd]  # not connected
  R1 = Resistor [tolerance=±10% resistance=4.7k package="0603 [SMD]"]  # not connected

nets:
  N1: M1.B12, DHT22.2
  N2: M1.B13, PIR_sensor.2
  N3: M1.B8, Buzzer.pin2
  N4: M1.G, Buzzer.pin1

notes:
  WOKWI PIN MAP — Blue Pill STM32F103C8T6
  Rails: 3V3 + common GND.
  DHT22: VCC=3V3, DATA=PB12, GND; pull-up DATA–3V3=5.1 kΩ.
  PIR: VCC=3V3, OUT=PB13, GND.
  SSD1306 OLED: VCC=3V3, GND, SCL=PB6, SDA=PB7 (0x3C).
  LDR: VCC=3V3, AO=PA0, GND.
  KY-040: CLK=PA1, DT=PA2, VCC=3V3, GND; SW unused.
  Buzzer: signal=PB8, other lead=GND.
  UART: PA9 TX→serial RX; PA10 RX unused.
  Fritzing library lacks exact sensor symbols; labeled headers are connector stand-ins. Resistor symbol is 4.7 kΩ ±10% (nearest library value); Wokwi uses 5.1 kΩ.
